# Fritzing sketch Sketch (saved by Fritzing 0.9.3b)

parts:
  BeerTempLogger = Arduino Uno (Rev3)
  R1 = Resistor [tolerance=±5% resistance=220 package=THT]
  T1 = LM35 Temperature Sensor [package="TO92 [THT]"]
  LED1 = LED - 5mm [color="Blue (430nm)" package="5 mm [THT]"]
  LED2 = LED - 5mm [color="Green (555nm)" package="5 mm [THT]"]
  LED3 = LED - 5mm [color="Red (633nm)" package="5 mm [THT]"]
  R2 = Resistor [tolerance=±5% resistance=220 package=THT]
  R3 = Resistor [tolerance=±5% resistance=220 package=THT]

nets:
  N1: BeerTempLogger.A0, T1.Vout
  GND: BeerTempLogger.GND, R1.Pin_1, T1.GND, R2.Pin_1, R3.Pin_1
  N2: BeerTempLogger.D2, LED3.anode
  N3: BeerTempLogger.D3_PWM, LED2.anode
  N4: BeerTempLogger.D4, LED1.anode
  N5: BeerTempLogger.5V, T1.+Vs
  N6: R1.Pin_0, LED1.cathode
  N7: LED2.cathode, R2.Pin_0
  N8: LED3.cathode, R3.Pin_0
